// Logisim project Lab0.circ as structural Verilog: 1 circuit, main circuit main
// x
module main (
  input  x,
  input  y,
  output x_prime,
  output xy,
  output x_y,
  output xy_2,
  output x_y_2,
  output x_y_3,
  output x_y_4
);

  not Not (x_prime, x);
  and And (xy, x, y);
  or Or (x_y, x, y);
  and And_2 (xy_2, x, y);
  or Or_2 (x_y_2, x, y);
  xnor xy__prime (x_y_3, x, y);
  xnor x_y__prime (x_y_4, x, y);

  // Notes on the sheet:
  //   A label
endmodule
