// Logisim project Class_Work.circ as structural Verilog: 3 circuits, main circuit main
module main (
  input  x_prime,
  input  y,
  input  z,
  output x_prime_y_z
);

  wire X_prime_out, y_z_out;

  not u_X_prime (X_prime_out, x_prime);
  and y_z (y_z_out, y, z);
  or or_1 (x_prime_y_z, X_prime_out, y_z_out);

  // Notes on the sheet:
  //   Inputs
  //   Circuit Diagram
  //   Output
endmodule

module Majority (
  input  x,
  input  y,
  input  z,
  output Majority
);

  wire x_prime_y_z_out, x_y_prime_z_2_out, x_y_prime_z_out, x_y_z_prime_out;

  and x_prime_y_z (x_prime_y_z_out, ~x, y, z);  // AND_Gate
  and x_y_prime_z (x_y_prime_z_out, x, ~y, z);  // AND_Gate
  and x_y_z_prime (x_y_z_prime_out, x, y, ~z);  // AND_Gate
  and x_y_prime_z_2 (x_y_prime_z_2_out, x, y, z);
  or or_1 (Majority, x_prime_y_z_out, x_y_prime_z_out, x_y_z_prime_out, x_y_prime_z_2_out);

  // Notes on the sheet:
  //   Inputs
  //   Outputs
endmodule

module Majority_G (
  input  x,
  input  y,
  input  z,
  output Majority
);

  wire and_1_out, and_2_out, and_3_out;

  and and_1 (and_1_out, y, z);
  and and_2 (and_2_out, x, z);
  and and_3 (and_3_out, x, y);
  or or_1 (Majority, and_1_out, and_2_out, and_3_out);
endmodule
