// Logisim project Class_Work2.circ as structural Verilog: 1 circuit, main circuit main
module main (
  input  s_prime,
  input  r_prime,
  input  in_3,
  input  [7:0] in_4,
  input  [7:0] in_5,
  input  [7:0] in_6,
  output q,
  output q_prime,
  output q_2,
  output q_prime_2
);

  wire clock_1_out;
  wire [7:0] register_1_q;

  Clock clock_1 (.out(clock_1_out));
  nand nand_1 (q, s_prime, q_prime);
  nand nand_2 (q_prime, q, r_prime);
  D_Flip_Flop d_ff_1 (.clk(clock_1_out), .D(in_3), .Q(q_2), .Qn(q_prime_2));  // open: preset, en, reset
  Register register_1 (.D(in_4), .Q(register_1_q), .clk(clock_1_out));  // open: en, clr
  ROM rom_1 (.addr(in_4), .data(in_6));  // open: sel
  Hex_Digit_Display hex_digit_display_1 (.value(register_1_q[7:4]));  // open: dp
  Hex_Digit_Display hex_digit_display_2 (.value(register_1_q[3:0]));  // open: dp

  // Notes on the sheet:
  //   Inputs
  //   Wiring ->Clock
  //   (SR)' NAND latch
  //   Memory->D flip-flop
  //   Outputs
endmodule
