// Logisim project Lab2.circ as structural Verilog: 1 circuit, main circuit main
module main (
  input  B,
  input  A,
  output out_3
);

  wire not_1_out;
  wire [1:1] undriven;

  not not_1 (not_1_out, B);
  Multiplexer #(.select(2), .enable("false")) multiplexer_1 (
    .in0(B), .in2(not_1_out), .out(out_3), .sel({undriven[1], A}));  // open: in1, in3
  // Pins of 1 and 2 bits meet at {undriven[1], A}
endmodule
