// Logisim project Lab2_classwork.circ as structural Verilog: 2 circuits, main circuit main
module main (
  input  Wiring__Pin
);

  wire clock_1_out;
  wire [1:0] circuit_1_n0, register_1_q;

  circuit circuit_1 (
    .s1(register_1_q[1]), .s0(register_1_q[0]), .\input (Wiring__Pin), .n1(circuit_1_n0[1]),
    .n0(circuit_1_n0[0]));
  Clock clock_1 (.out(clock_1_out));
  Register #(.width(2)) register_1 (.D(circuit_1_n0), .Q(register_1_q), .clk(clock_1_out));  // open: en, clr
  Hex_Digit_Display hex_digit_display_1 (.value({2'b00, register_1_q}));  // open: dp

  // Notes on the sheet:
  //   Window->Combinational Analysis
  //   Wiring->Clock
  //   Memory->Register
  //   I/O->Display
  //   Wiring->Constant
endmodule

module circuit (
  input  s1,
  input  s0,
  input  \input ,
  output n1,
  output n0
);

  wire and_1_out, and_2_out, and_3_out, and_4_out, and_5_out, not_1_out, not_2_out, not_3_out, not_4_out,
       not_5_out;

  not not_1 (not_1_out, s0);
  not not_2 (not_2_out, s1);
  not not_3 (not_3_out, s0);
  not not_4 (not_4_out, \input );
  not not_5 (not_5_out, s0);
  and and_1 (and_1_out, not_1_out, \input );
  and and_2 (and_2_out, not_2_out, s0);
  and and_3 (and_3_out, not_3_out, not_4_out);
  and and_4 (and_4_out, s0, \input );
  and and_5 (and_5_out, s1, not_5_out);
  or or_1 (n1, and_1_out, and_2_out);
  or or_2 (n0, and_3_out, and_4_out, and_5_out);
  Register register_1 ();  // open: D, en, Q, clk, clr
endmodule
